// Logisim project cpu030_intc_1.circ as structural Verilog: 1 circuit, main circuit main
module main (
  input  D0,
  input  RESETb,
  input  I0b,
  input  I1b,
  input  I2b,
  input  I3b,
  input  I4b,
  input  I5b,
  input  I6b,
  input  IACK,
  input  DSb,
  input  CSb,
  input  RW
);

  wire and_1_out, and_2_out, and_3_out, and_4_out, and_5_out, and_6_out, and_7_out, and_8_out, and_9_out,
       and_10_out, and_11_out, and_12_out, and_13_out, and_14_out, and_15_out, and_16_out, AVEC, BERR, CS,
       DS, DSACK0, ENAB, FFC, I0, I1, I2, I3, I4, I5, I6, IPL0, IPL1, IPL2, nI0, nI1, nI2, nI3, nI4, nI5,
       nI6, nIPL0, nIPL1, nIPL2, not_1_out, W;

  not not_1 (not_1_out, RESETb);
  not not_2 (I0, I0b);
  not not_3 (I1, I1b);
  not not_4 (I2, I2b);
  not not_5 (I3, I3b);
  not not_6 (I4, I4b);
  not not_7 (I5, I5b);
  not not_8 (I6, I6b);
  not not_9 (DS, DSb);
  not not_10 (CS, CSb);
  not not_11 (W, RW);
  and and_1 (and_1_out, ENAB, nI0, nI1, nI2, nI3, nI4, nI5, I6);
  and and_2 (and_2_out, ENAB, nI0, nI1, nI2, nI3, I4);
  and and_3 (and_3_out, ENAB, nI0, nI1, I2);
  and and_4 (and_4_out, ENAB, I0);
  and and_5 (and_5_out, ENAB, nI0, nI1, nI2, nI3, nI4, I5);
  and and_6 (and_6_out, ENAB, nI0, nI1, nI2, nI3, I4);
  and and_7 (and_7_out, ENAB, nI0, I1);
  and and_8 (and_8_out, ENAB, I0);
  and and_9 (and_9_out, ENAB, nI0, nI1, nI2, I3);
  and and_10 (and_10_out, ENAB, nI0, nI1, I2);
  and and_11 (and_11_out, ENAB, nI0, I1);
  and and_12 (and_12_out, ENAB, I0);
  D_Flip_Flop d_ff_1 (.D(D0), .clk(FFC), .Q(ENAB), .reset(not_1_out));  // open: Qn, preset
  not not_12 (nI0, I0);
  not not_13 (nI1, I1);
  not not_14 (nI2, I2);
  not not_15 (nI3, I3);
  not not_16 (nI4, I4);
  not not_17 (nI5, I5);
  not not_18 (nI6, I6);
  and and_13 (and_13_out, CS, DS, W);
  or or_1 (IPL0, and_1_out, and_2_out, and_3_out, and_4_out);
  not not_19 (nIPL0, IPL0);
  or or_2 (IPL1, and_5_out, and_6_out, and_7_out, and_8_out);
  not not_20 (nIPL1, IPL1);
  or or_3 (IPL2, and_9_out, and_10_out, and_11_out, and_12_out);
  not not_21 (nIPL2, IPL2);
  not not_22 (FFC, and_13_out);
  and and_14 (and_14_out, IACK, IPL0);
  and and_15 (and_15_out, IACK, IPL1);
  and and_16 (and_16_out, IACK, IPL2);
  Hex_Digit_Display hex_digit_display_1 (.value({1'b0, IPL2, IPL1, IPL0}));  // open: dp
  LED led_1 (.in(AVEC));
  LED led_2 (.in(BERR));
  LED led_3 (.in(DSACK0));
  or or_4 (AVEC, and_14_out, and_15_out, and_16_out);
  and and_17 (DSACK0, CS, DS);
  and and_18 (BERR, IACK, nIPL0, nIPL1, nIPL2);

  // Other names for the same wires on the sheet: R = RW
endmodule
